// Logisim project alu_unit.circ as structural Verilog: 1 circuit, main circuit main
module main (
  input  [31:0] BusA,
  input  [31:0] BusB,
  input  isLogic,
  input  [31:0] in_4,
  input  [31:0] in_5,
  input  [1:0] f,
  output [31:0] AluOut,
  output ZeroFlag
);

  wire comparator_1_eq, comparator_1_gt;
  wire [31:0] adder_1_out, adder_2_out, and_1_out, and_2_out, bit_extender_1_out, bit_extender_2_out,
       multiplexer_1_out, multiplexer_2_out, not_1_out, or_1_out, xor_1_out;

  assign and_1_out = BusA & BusB;  // AND_Gate and_1, 32 bits wide
  assign and_2_out = ~BusA & BusB;  // AND_Gate and_2, 32 bits wide
  assign or_1_out = BusA | BusB;  // OR_Gate or_1, 32 bits wide
  assign xor_1_out = BusA ^ BusB;  // XOR_Gate xor_1, 32 bits wide
  Adder #(.width(32)) adder_1 (.a(BusA), .b(BusB), .out(adder_1_out), .cin(1'b0));  // open: cout
  assign not_1_out = ~BusA;  // NOT_Gate not_1, 32 bits wide
  Adder #(.width(32)) adder_2 (.a(not_1_out), .b(BusB), .out(adder_2_out), .cin(1'b1));  // open: cout
  Comparator #(.width(32)) comparator_1 (
    .a(adder_2_out), .b(in_5), .gt(comparator_1_gt), .eq(comparator_1_eq));  // open: lt
  assign bit_extender_1_out = {{31{1'b0}}, comparator_1_gt};  // Bit_Extender bit_extender_1
  assign bit_extender_2_out = {{31{1'b0}}, comparator_1_eq};  // Bit_Extender bit_extender_2
  Multiplexer #(.select(2), .width(32)) multiplexer_1 (
    .in0(and_1_out), .in1(and_2_out), .in2(or_1_out), .in3(xor_1_out), .out(multiplexer_1_out), .sel(f));
  Multiplexer #(.select(2), .width(32)) multiplexer_2 (
    .in0(adder_1_out), .in1(adder_2_out), .in2(bit_extender_2_out), .in3(bit_extender_1_out),
    .out(multiplexer_2_out), .sel(f));
  Multiplexer #(.width(32)) multiplexer_3 (
    .in0(multiplexer_1_out), .in1(multiplexer_2_out), .out(AluOut), .sel(isLogic));
  Comparator #(.width(32)) comparator_2 (.a(AluOut), .b(in_4), .eq(ZeroFlag));  // open: gt, lt

  // Notes on the sheet:
  //   BusA: initial=0x12345678
endmodule
