// Logisim project datapath.circ as structural Verilog: 1 circuit, main circuit main
module main (
  input  in_1
);

  wire alu_1_out_11, alu_1_zeroflag, alucontrolsignals_1_isnotlogic, alucontrolsignals_1_isnotshift,
       clock_1_out;
  wire [1:0] alucontrolsignals_1_shiftop, main_control_input_splitter_1_f2;
  wire [2:0] main_control_input_splitter_1_a3, main_control_input_splitter_1_b3,
       main_control_input_splitter_1_d3, multiplexer_1_out;
  wire [4:0] main_control_input_splitter_1_imm5, main_control_input_splitter_1_op5;
  wire [10:0] main_control_input_splitter_1_imm11, shifter_1_out;
  wire [15:0] rom_1_data;
  wire [19:0] adder_1_out, bit_extender_1_out, register_1_q;
  wire [31:0] alu_1_aluout, bit_extender_2_out, DataMemory_dout, multiplexer_2_out, multiplexer_3_out,
       registerfile_1_busa, registerfile_1_busb;

  pc_control pc_control_1 (
    .Zero(alu_1_zeroflag), .LT(alu_1_out_11), .EQ(alu_1_zeroflag), .OpCode(main_control_input_splitter_1_op5));  // open: PCSrc_0, PCSrc_2, PCSrc_3, PCSrc_1
  Clock clock_1 (.out(clock_1_out));
  Register #(.width(20)) register_1 (.D(adder_1_out), .en(1'b1), .clk(clock_1_out), .Q(register_1_q), .clr(in_1));
  Adder #(.width(20)) adder_1 (.a(register_1_q), .b(20'h2), .out(adder_1_out));  // open: cin, cout
  ROM #(.addrWidth(20), .dataWidth(16)) rom_1 (.addr(register_1_q), .data(rom_1_data));
  assign bit_extender_1_out = {{9{shifter_1_out[10]}}, shifter_1_out};  // Bit_Extender bit_extender_1
  Shifter #(.width(11)) shifter_1 (.in(main_control_input_splitter_1_imm11), .\dist (4'b0001), .out(shifter_1_out));
  Main_Control_Input_Splitter main_control_input_splitter_1 (
    .in_1(rom_1_data), .f2(main_control_input_splitter_1_f2), .d3(main_control_input_splitter_1_d3),
    .Imm5(main_control_input_splitter_1_imm5), .b3(main_control_input_splitter_1_b3),
    .a3(main_control_input_splitter_1_a3), .Imm11(main_control_input_splitter_1_imm11),
    .Op5(main_control_input_splitter_1_op5));
  Multiplexer #(.width(3)) multiplexer_1 (
    .in0(main_control_input_splitter_1_b3), .in1(main_control_input_splitter_1_d3), .out(multiplexer_1_out));  // open: sel
  assign bit_extender_2_out = {{27{main_control_input_splitter_1_imm5[4]}}, main_control_input_splitter_1_imm5};  // Bit_Extender bit_extender_2
  registerFile registerfile_1 (
    .BusW(multiplexer_3_out), .RA(main_control_input_splitter_1_a3), .RW(multiplexer_1_out),
    .BusA(registerfile_1_busa), .BusB(registerfile_1_busb));  // open: RB, RegWrite, clk
  Multiplexer #(.width(32)) multiplexer_2 (
    .in0(registerfile_1_busb), .in1(bit_extender_2_out), .out(multiplexer_2_out));  // open: sel
  AluControlSignals alucontrolsignals_1 (
    .in_1(rom_1_data), .isNotLogic(alucontrolsignals_1_isnotlogic),
    .IsNotShift(alucontrolsignals_1_isnotshift), .ShiftOp(alucontrolsignals_1_shiftop));
  ALU alu_1 (
    .BusA(registerfile_1_busa), .BusB(multiplexer_2_out), .ShiftOp(alucontrolsignals_1_shiftop),
    .IsNotShift(alucontrolsignals_1_isnotshift), .isNotLogic(alucontrolsignals_1_isnotlogic),
    .f(main_control_input_splitter_1_f2), .AluOut(alu_1_aluout), .ZeroFlag(alu_1_zeroflag),
    .out_11(alu_1_out_11));  // open: in_6, in_7
  RAM #(.addrWidth(18), .dataWidth(32)) DataMemory (
    .addr(alu_1_aluout[19:2]), .din(registerfile_1_busb), .dout(DataMemory_dout));  // open: we, oe, clk
  Multiplexer #(.width(32)) multiplexer_3 (
    .in0(alu_1_aluout), .in1(DataMemory_dout), .out(multiplexer_3_out));  // open: sel

  // Notes on the sheet:
  //   contents of rom_1 (hex, n*v repeats v):
  //   2222 2222 2222
endmodule
