// Logisim project pc.circ as structural Verilog: 1 circuit, main circuit Program_Counter
module Program_Counter (
  input  in_1
);

  wire clock_1_out;
  wire [19:0] adder_1_out, register_1_q, undriven;

  Register #(.width(20)) register_1 (.D(undriven), .en(1'b1), .clk(clock_1_out), .Q(register_1_q), .clr(in_1));
  Clock clock_1 (.out(clock_1_out));
  Adder #(.width(20)) adder_1 (.a(register_1_q), .b(20'h2), .out(adder_1_out));  // open: cin, cout
endmodule
